// Logisim project addder.circ as structural Verilog: 1 circuit, main circuit main
module main (
  input  X0,
  input  X1,
  input  X2,
  input  C0,
  input  X3,
  input  Y0,
  input  Y1,
  input  Y2,
  input  Y3,
  output S0,
  output C1,
  output S1,
  output C2,
  output S2,
  output C3,
  output S3,
  output C4
);

  wire and_1_out, and_2_out, and_3_out, and_4_out, and_5_out, and_6_out, and_7_out, and_8_out, and_9_out,
       and_10_out, and_11_out, and_12_out, and_13_out, and_14_out, or_1_out, or_2_out, or_3_out, or_6_out,
       or_7_out, or_9_out, xor_1_out, xor_2_out, xor_3_out, xor_4_out;

  Hex_Digit_Display hex_digit_display_1 (.value({S3, S2, S1, S0}));  // open: dp
  xor xor_1 (xor_1_out, X0, Y0);
  xor xor_2 (xor_2_out, X1, Y1);
  xor xor_3 (xor_3_out, X2, Y2);
  and and_1 (and_1_out, X2, Y2);
  xor xor_4 (xor_4_out, Y3, X3);
  and and_2 (and_2_out, Y3, X3);
  and and_3 (and_3_out, X0, Y0);
  and and_4 (and_4_out, X1, Y1);
  and and_5 (and_5_out, xor_1_out, C0);
  and and_6 (and_6_out, xor_1_out, C0);
  and and_7 (and_7_out, xor_1_out, C0);
  and and_8 (and_8_out, xor_1_out, C0);
  or or_1 (or_1_out, and_5_out, and_3_out);
  or or_2 (or_2_out, and_6_out, and_3_out);
  or or_3 (or_3_out, and_3_out, and_7_out);
  xor xor_5 (S0, xor_1_out, C0);
  or or_4 (C1, and_3_out, and_8_out);
  and and_9 (and_9_out, or_1_out, xor_2_out);
  and and_10 (and_10_out, xor_2_out, or_2_out);
  and and_11 (and_11_out, xor_2_out, or_3_out);
  or or_5 (C2, and_4_out, and_9_out);
  or or_6 (or_6_out, and_10_out, and_4_out);
  or or_7 (or_7_out, and_11_out, and_4_out);
  xor xor_6 (S1, C1, xor_2_out);
  xor xor_7 (S2, xor_3_out, C2);
  or or_8 (C3, and_1_out, and_12_out);
  and and_12 (and_12_out, or_6_out, xor_3_out);
  and and_13 (and_13_out, xor_3_out, or_7_out);
  xor xor_8 (S3, xor_4_out, C3);
  or or_9 (or_9_out, and_1_out, and_13_out);
  and and_14 (and_14_out, or_9_out, xor_4_out);
  or or_10 (C4, and_2_out, and_14_out);
endmodule
