// Logisim project shift_register.circ as structural Verilog: 1 circuit, main circuit main
module main (
  input  in_1,
  input  Reset,
  input  in_3,
  input  Reset_2,
  output out_5,
  output out_6,
  output out_7,
  output out_8,
  output out_9,
  output out_10,
  output out_11,
  output out_12
);

  wire Clock_2_out, Clock_out;

  Clock Clock (.out(Clock_out));
  Clock Clock_2 (.out(Clock_2_out));
  D_Flip_Flop d_ff_1 (.D(in_1), .clk(Clock_out), .Q(out_5), .reset(Reset));  // open: Qn, preset
  D_Flip_Flop d_ff_2 (.D(in_3), .clk(Clock_2_out), .Q(out_12), .reset(Reset_2));  // open: Qn, preset
  D_Flip_Flop d_ff_3 (.D(out_5), .clk(Clock_out), .Q(out_6), .reset(Reset));  // open: Qn, preset
  D_Flip_Flop d_ff_4 (.D(out_12), .clk(Clock_2_out), .Q(out_11), .reset(Reset_2));  // open: Qn, preset
  D_Flip_Flop d_ff_5 (.D(out_6), .clk(Clock_out), .Q(out_7), .reset(Reset));  // open: Qn, preset
  D_Flip_Flop d_ff_6 (.D(out_11), .clk(Clock_2_out), .Q(out_10), .reset(Reset_2));  // open: Qn, preset
  D_Flip_Flop d_ff_7 (.D(out_7), .clk(Clock_out), .Q(out_8), .reset(Reset));  // open: Qn, preset
  D_Flip_Flop d_ff_8 (.D(out_10), .clk(Clock_2_out), .Q(out_9), .reset(Reset_2));  // open: Qn, preset
endmodule
