// Logisim project universal_shift_register.circ as structural Verilog: 2 circuits, main circuit main
module main (
  input  Parrallel_input,
  input  Parrallel_input_2,
  input  Parrallel_input_3,
  input  Parrallel_input_4,
  input  left_shift,
  input  right_shift,
  input  s0,
  input  s1,
  input  Reset,
  output out_10,
  output out_11,
  output out_12,
  output out_13
);

  wire Clock_out, mux_1_output, mux_2_output, mux_3_output, mux_4_output;

  Clock Clock (.out(Clock_out));
  mux mux_1 (
    .d0(out_10), .d1(right_shift), .d2(out_11), .d3(Parrallel_input), .s0(s0), .s1(s1),
    .\output (mux_1_output));
  D_Flip_Flop d_ff_1 (.D(mux_1_output), .clk(Clock_out), .Q(out_10), .reset(Reset));  // open: Qn, preset
  mux mux_2 (.d0(out_11), .d1(out_10), .d2(out_12), .d3(Parrallel_input_2), .s0(s0), .s1(s1), .\output (mux_2_output));
  D_Flip_Flop d_ff_2 (.D(mux_2_output), .clk(Clock_out), .Q(out_11), .reset(Reset));  // open: Qn, preset
  mux mux_3 (.d0(out_12), .d1(out_11), .d2(out_13), .d3(Parrallel_input_3), .s0(s0), .s1(s1), .\output (mux_3_output));
  D_Flip_Flop d_ff_3 (.D(mux_3_output), .clk(Clock_out), .Q(out_12), .reset(Reset));  // open: Qn, preset
  D_Flip_Flop d_ff_4 (.D(mux_4_output), .clk(Clock_out), .Q(out_13), .reset(Reset));  // open: Qn, preset
  mux mux_4 (
    .d0(out_13), .d1(out_12), .d2(left_shift), .d3(Parrallel_input_4), .s0(s0), .s1(s1),
    .\output (mux_4_output));
endmodule

module mux (
  input  s0,
  input  s1,
  input  d0,
  input  d1,
  input  d2,
  input  d3,
  output \output 
);

  wire and_1_out, and_2_out, and_3_out, and_4_out, not_1_out, not_2_out;

  not not_1 (not_1_out, s0);
  not not_2 (not_2_out, s1);
  and and_1 (and_1_out, not_1_out, not_2_out, d0);
  and and_2 (and_2_out, s0, not_2_out, d1);
  and and_3 (and_3_out, not_1_out, s1, d2);
  and and_4 (and_4_out, s0, s1, d3);
  or or_1 (\output , and_1_out, and_2_out, and_3_out, and_4_out);
endmodule
